# Fritzing sketch Montage (saved by Fritzing 0.9.2b)
breadboards: 1

parts:
  U1 = MCP41xxx [package=so08]  # not connected
  Composant1 = Arduino Mega ADK (Rev3)
  J1 = Infrared Proximity Sensor
  Q1 = MOSFET-NCHANNEL [package=to220v]  # not connected

nets:
  N1: Composant1.A9, J1.Vout
  5V: Composant1.5V, J1.Vcc
  GND: Composant1.GND, J1.GND
